# Fritzing sketch FinalProjectFritzing (saved by Fritzing 0.9.3b)
breadboards: 1

parts:
  S1 = Pushbutton [package="[THT]"]
  S2 = Pushbutton [package="[THT]"]
  S3 = Pushbutton [package="[THT]"]
  R1 = Resistor [tolerance=±5% resistance=220 package=THT]
  R2 = Resistor [tolerance=±5% resistance=220 package=THT]
  R3 = Resistor [tolerance=±5% resistance=220 package=THT]
  LED1 = LED - 5mm [color="Red (633nm)" package="5 mm [THT]"]
  LED2 = LED - 5mm [color="Green (555nm)" package="5 mm [THT]"]
  LED3 = LED - 5mm [color="Blue (430nm)" package="5 mm [THT]"]
  R4 = Resistor [tolerance=±5% resistance=220 package=THT]
  R5 = Resistor [tolerance=±5% resistance=220 package=THT]
  R6 = Resistor [tolerance=±5% resistance=220 package=THT]
  Part1 = Arduino Uno (Rev3)
  J1 = Piezo Speaker

nets:
  N1: S1.Pin_1, S1.Pin_2, R1.Pin_0, Part1.D13/SCK
  N2: S1.Pin_3, S1.Pin_4, S2.Pin_3, S2.Pin_4, S3.Pin_3, S3.Pin_4, LED1.cathode, LED2.cathode, LED3.cathode, Part1.GND, J1.pin1
  N3: S2.Pin_1, S2.Pin_2, R2.Pin_0, Part1.D12/MISO
  N4: S3.Pin_1, S3.Pin_2, R3.Pin_0, Part1.D11_PWM/MOSI
  N5: R1.Pin_1, R2.Pin_1, R3.Pin_1, Part1.5V
  N6: LED1.anode, R6.Pin_1
  N7: LED2.anode, R5.Pin_1
  N8: LED3.anode, R4.Pin_1
  N9: R4.Pin_0, Part1.D1/TX
  N10: R5.Pin_0, Part1.D2
  N11: R6.Pin_0, Part1.D3_PWM
  N12: Part1.D8, J1.pin2
